// Logisim project Group2.circ as structural Verilog
module project_ao (
  input  [15:0] A,
  input  [15:0] B,
  input  [3:0] selector,
  output [15:0] result
);

  wire [15:0] adder_1_out, and_1_out, divider_1_out, divider_1_rem, multiplier_1_out, negator_1_out,
       negator_2_out, or_1_out, shifter_1_out, shifter_2_out, shifter_3_out, shifter_4_out, subtractor_1_out,
       xor_1_out;

  Adder #(.width(16)) adder_1 (.a(A), .b(B), .out(adder_1_out));  // open: cin, cout
  assign and_1_out = A & B;  // AND_Gate and_1, 16 bits wide
  assign or_1_out = A | B;  // OR_Gate or_1, 16 bits wide
  assign xor_1_out = A ^ B;  // XOR_Gate xor_1, 16 bits wide
  Divider #(.width(16)) divider_1 (.a(A), .b(B), .out(divider_1_out), .rem(divider_1_rem));  // open: upper
  Multiplier #(.width(16)) multiplier_1 (.a(A), .b(B), .out(multiplier_1_out));  // open: cin, cout
  Subtractor #(.width(16)) subtractor_1 (.a(A), .b(B), .out(subtractor_1_out));  // open: bin, bout
  Shifter #(.width(16)) shifter_1 (.in(A), .\dist (4'b0010), .out(shifter_1_out));
  Shifter #(.width(16)) shifter_2 (.in(B), .\dist (4'b0010), .out(shifter_2_out));
  Shifter #(.shift("lr"), .width(16)) shifter_3 (.in(A), .\dist (4'b0010), .out(shifter_3_out));
  Shifter #(.shift("lr"), .width(16)) shifter_4 (.in(B), .\dist (4'b0010), .out(shifter_4_out));
  Negator #(.width(16)) negator_1 (.in(A), .out(negator_1_out));
  Negator #(.width(16)) negator_2 (.in(B), .out(negator_2_out));
  Multiplexer #(.select(4), .width(16)) multiplexer_1 (
    .in0(adder_1_out), .in1(and_1_out), .in2(or_1_out), .in3(xor_1_out), .in4(divider_1_out),
    .in5(divider_1_rem), .in6(multiplier_1_out), .in7(subtractor_1_out), .in8(shifter_1_out),
    .in9(shifter_2_out), .in10(shifter_3_out), .in11(shifter_4_out), .in12(negator_1_out),
    .in13(negator_2_out), .out(result), .sel(selector));  // open: in14, in15
endmodule

module project_ro (
  input  [2:0] selector,
  output result
);

  wire comparator_1_eq, comparator_1_gt, comparator_1_lt;
  wire [7:0] undriven, undriven_2;

  Comparator #(.mode("unsigned")) comparator_1 (
    .a(undriven), .b(undriven_2), .gt(comparator_1_gt), .eq(comparator_1_eq), .lt(comparator_1_lt));
  Multiplexer #(.select(3)) multiplexer_1 (
    .out(result), .sel(selector));  // open: in0, in1, in2, in3, in4, in5, in6, in7

  // Notes on the sheet:
  //   010: =
  //   011: !=
  //   100: <=
  //   101: <
endmodule
